# Fritzing sketch SensorPresenca (saved by Fritzing 0.9.3b)
breadboards: 1
stripboards: 1

parts:
  U1 = ESP8266 WiFi Module [part_number=ESP8266]
  VCC2 = Battery  # not connected
  VCC1 = Battery
  PIR1 = PIR sensor

nets:
  N1: U1.RXD, U1.GPIO_0, U1.GPIO_2, U1.GND
  N2: U1.VCC, U1.RST, U1.CH_PD
  N3: VCC1.-, PIR1.GND
  N4: VCC1.+, PIR1.VDD

notes:
  CP-RST-IO0-IO2-TXH-RXH-3V3-GND-GND-VIN
  3 Pilhas, cada uma com 1,5V, somando 4,5V
  VIN-IO0-GND

custom parts:
  ESP8266 WiFi Module: Generic WiFi Module based on the ESP8266 with onboard PCB antenna and UART communications
